# Fritzing sketch AX12-Servo (saved by Fritzing 0.8.5b)
breadboards: 1

parts:
  J1 = Basic Servo  # not connected
  Part1 = Arduino Mega 2560 (Rev3)
  J2 = Basic Servo

nets:
  GND: Part1.GND, J2.gnd

notes:
  Source
  GND
  12V
  Green - Tx
  Yellow - Rx
