# Fritzing sketch HYT271-HumTemp (saved by Fritzing 0.8.5b)
breadboards: 1

parts:
  Part1 = Arduino Mega 2560 (Rev3)
  R1 = Resistor [tolerance=±5% resistance=2.2k package=THT]
  R2 = Resistor [tolerance=±5% resistance=2.2k package=THT]
  Part2 = HTU21D-F Temperature + Humidity Sensor

nets:
  N1: Part1.D21/SCL, R1.Pin_1, Part2.SCL
  N2: Part1.D20/SDA, R2.Pin_1, Part2.SDA
  5V: Part1.5V, R1.Pin_0, R2.Pin_0, Part2.VIN
  GND: Part1.GND, Part2.GND

notes:
  HYT271
  Red - VDD
  Blue - SDA
  Yellow - SCL
  Black - GND

custom parts:
  HTU21D-F Temperature + Humidity Sensor: This I2C digital humidity sensor is an accurate and intelligent alternative to the much simpler Humidity and Temperature Sensor - SHT15 Breakout It has a typical accuracy of ±2% with an operating range that's optimized from 5% to 95% RH. Operation outside this range is still possible - just the accuracy might drop a bit. The temperature output has an accuracy of ±1°C from -30~90°C. If you're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
