# Fritzing sketch LEDarray (saved by Fritzing 0.8.5b)

parts:
  IC5 = DIP - 8 pins [chip_label=IC package="DIP (Dual Inline) [THT]"]
  IC6 = DIP - 8 pins [chip_label=IC package="DIP (Dual Inline) [THT]"]
  IC7 = DIP - 8 pins [chip_label=IC package="DIP (Dual Inline) [THT]"]
  IC8 = DIP - 8 pins [chip_label=IC package="DIP (Dual Inline) [THT]"]
  IC9 = DIP - 8 pins [chip_label=IC package="DIP (Dual Inline) [THT]"]
  IC10 = DIP - 8 pins [chip_label=IC package="DIP (Dual Inline) [THT]"]

nets:
  N1: IC5.White+, IC6.White-
  N2: IC5.Red+, IC8.Red-
  N3: IC5.Blue+, IC8.Blue-
  N4: IC6.Red+, IC7.Red-
  N5: IC6.Blue+, IC7.Blue-
  N6: IC7.Red+, IC9.Red-
  N7: IC7.White-, IC8.White+
  N8: IC7.Blue+, IC9.Blue-
  N9: IC8.Red+, IC10.Red-
  N10: IC8.Blue+, IC10.Blue-
  N11: IC9.White-, IC10.White+

custom parts:
  DIP - 8 pins: A DIP stand-in part for whatever IC you want. With 8 pins on a 300mil dual inline package (DIP) footprint.
