# Fritzing sketch T6613-CO2 (saved by Fritzing 0.8.5b)

parts:
  Part1 = Arduino Mega 2560 (Rev3)
  MH-Z1 = MH-Z14 [part_number=MH-Z14]

nets:
  N1: Part1.D13_PWM, MH-Z1.11, MH-Z1.14
  N2: Part1.D12_PWM, MH-Z1.10, MH-Z1.13
  N3: Part1.5V, MH-Z1.15
  N4: Part1.GND, MH-Z1.3

custom parts:
  MH-Z14: MH-Z14 NDIR Infrared gas module is a common type, small size sensor, using non-dispersive infrared (NDIR) principle to detect the existence of CO2 in the air, with good selectivity, non-oxygen dependant, long life. Built-in temperature sensor can do temperature compensation; and it has digital output and analog voltage output.
