# Fritzing sketch HYT271-breadboard (saved by Fritzing 0.8.5b)
breadboards: 1

parts:
  Part1 = Arduino Mega 2560 (Rev3)
  R1 = Resistor [tolerance=±5% resistance=220 package=THT]
  R2 = Resistor [tolerance=±5% resistance=220 package=THT]

nets:
  N1: Part1.D21/SCL, R2.Pin_1
  N2: Part1.D20/SDA, R1.Pin_1
  N3: Part1.5V, R1.Pin_0, R2.Pin_0

notes:
  HYT271
  Red - VDD
  Blue - SDA
  Yellow - SCL
  Black - GND
